# Fritzing sketch arduino-weather-station (saved by Fritzing 0.9.3b)
breadboards: 1

parts:
  Componente1 = Arduino Uno (Rev3) - ICSP
  DHT1 = DHT22 Humidity and Temperature Sensor
  YL-83_-_Detection_Board1 = YL-83 Rain Sensor - Detection Board
  YL-83_-_Control_Board1 = YL-83 Rain Sensor - Control Board
  Part1 = ML8511 Breakout Board
  R1 = Resistor [tolerance=±5% resistance=1k package=THT]
  R2 = Resistor [tolerance=±5% resistance=1k package=THT]
  R3 = Resistor [tolerance=±5% resistance=1k package=THT]
  R4 = Resistor [tolerance=±5% resistance=220 package=THT]
  U1 = ESP8266 WiFi Module [part_number=ESP8266]

nets:
  N1: Componente1.A0, YL-83_-_Control_Board1.AO
  N2: Componente1.A1, Part1.OUT
  3V3: Componente1.A2, Componente1.3V3, Part1.3V3, Part1.EN, R4.Pin_0, U1.VCC
  N3: Componente1.D2, U1.TXD
  N4: Componente1.D3_PWM, R3.Pin_1
  N5: Componente1.D4, DHT1.DATA
  5V: Componente1.5V, DHT1.VDD, YL-83_-_Control_Board1.VCC
  GND: Componente1.GND, DHT1.GND, YL-83_-_Control_Board1.GND, Part1.GND, R1.Pin_0, U1.GND
  N6: YL-83_-_Detection_Board1.POS, YL-83_-_Control_Board1.POS
  N7: YL-83_-_Detection_Board1.NEG, YL-83_-_Control_Board1.NEG
  N8: R1.Pin_1, R2.Pin_0, U1.RXD
  N9: R2.Pin_1, R3.Pin_0
  N10: R4.Pin_1, U1.CH_PD

custom parts:
  YL-83 Rain Sensor - Detection Board: The YL-83 is a rain sensor that has more resistance when dry and less resistance when wet. The module runs at 5V.
  YL-83 Rain Sensor - Control Board: The YL-83 is a rain sensor that has more resistance when dry and less resistance when wet. The module runs at 5V.
  ML8511 Breakout Board: This breakout board uses the ML8511 UV (ultraviolet) light sensor. The ML8511 works best with light in the 280-390nm wavelengths. The board operates at 2.7 to 3.6V.
  ESP8266 WiFi Module: Generic WiFi Module based on the ESP8266 with onboard PCB antenna and UART communications
